# Fritzing sketch DeploymentLauncher (saved by Fritzing 0.9.2b)
breadboards: 1

parts:
  U1 = Arduino Uno (Rev3)
  S1 = Toggle Switch [package=THT]
  S2 = Toggle Switch [package=THT]
  S3 = Pushbutton [package=THT]
  D3 = LED - 5mm [color="Green (555nm)" package="5 mm [THT]"]
  R1 = Resistor [tolerance=±5% resistance=10k package=THT]
  R2 = Resistor [tolerance=±5% resistance=10k package=THT]
  R3 = Resistor [tolerance=±5% resistance=10k package=THT]
  D1 = LED - 5mm [color="White (6500K)" package="5 mm [THT]"]
  D2 = LED - 5mm [color="Red (633nm)" package="5 mm [THT]"]

nets:
  N1: U1.D8, D2.anode
  N2: U1.D11_PWM/MOSI, D1.anode
  N3: U1.D12/MISO, D3.anode
  N4: U1.D2, S1.L2, R1.Pin_0
  N5: U1.D4, S2.L2, R2.Pin_0
  N6: U1.D7, S3.leg1, R3.Pin_0
  N7: U1.5V, S1.COM, S2.COM, S3.leg0
  N8: U1.GND, D3.cathode, R1.Pin_1, R2.Pin_1, R3.Pin_1, D1.cathode, D2.cathode
